// Logisim project lab6ALU.circ as structural Verilog: 1 circuit, main circuit ALU
// LAB12-ALU
module ALU (
  input  [31:0] ALU_Source_1,
  input  [31:0] ALU_Source_2,
  input  [2:0] ALU_Control,
  output [31:0] ALU_Result
);

  wire [31:0] \and , \or , rotl, rotr, sll, sra, srl, \xor ;

  // Probe on ALU_Source_1
  // Probe on ALU_Source_2
  assign \and  = ALU_Source_1 & ALU_Source_2;  // AND_Gate and_1, 32 bits wide
  assign \or  = ALU_Source_1 | ALU_Source_2;  // OR_Gate or_1, 32 bits wide
  assign \xor  = ALU_Source_1 ^ ALU_Source_2;  // XOR_Gate xor_1, 32 bits wide
  Shifter #(.width(32)) shifter_1 (.in(ALU_Source_1), .\dist (ALU_Source_2[4:0]), .out(sll));
  Shifter #(.width(32), .shift("lr")) shifter_2 (.in(ALU_Source_1), .\dist (ALU_Source_2[4:0]), .out(srl));
  Shifter #(.width(32), .shift("ar")) shifter_3 (.in(ALU_Source_1), .\dist (ALU_Source_2[4:0]), .out(sra));
  Shifter #(.width(32), .shift("rl")) shifter_4 (.in(ALU_Source_1), .\dist (ALU_Source_2[4:0]), .out(rotl));
  Shifter #(.width(32), .shift("rr")) shifter_5 (.in(ALU_Source_1), .\dist (ALU_Source_2[4:0]), .out(rotr));
  // Probe on ALU_Result
  Multiplexer #(.select(3), .width(32)) multiplexer_1 (
    .in0(sll), .in1(srl), .in2(sra), .in3(rotl), .in4(rotr), .in5(\and ), .in6(\or ), .in7(\xor ),
    .out(ALU_Result), .sel(ALU_Control));  // open: en

  // Other names for the same wires on the sheet: control[2:0] = ALU_Control; result[31:0] = ALU_Result;
  //   source1[31:0] = ALU_Source_1; source2[31:0] = ALU_Source_2

  // Notes on the sheet:
  //   DO NOT CROSS WIRES
  //   OVER THIS BOX
  //   DO NOT CROSS WIRES
  //   OVER THIS BOX
  //   COMPUTE ALL POSSIBLE OPERATIONS
  //   * YOUR CIRCUIT HERE *
  //   DO NOT CROSS WIRES
  //   OVER THIS BOX
  //   DO NOT CROSS WIRES
  //   OVER THIS BOX
  //   SELECT THE REQUESTED RESULT
  //   * YOUR CIRCUIT HERE *
  //   DO NOT CROSS WIRES
  //   OVER THIS BOX
endmodule
