// Logisim project lab6file.circ as structural Verilog
module Ex1 (
  input  [7:0] In,
  output Out1,
  output [7:0] Out2
);

  not not_1 (Out2[7], In[7]);
  and and_1 (Out1, In[0], In[7]);

  assign Out2[6:0] = In[6:0];
endmodule

module rotr (
  input  [3:0] in_1,
  input  [15:0] in_2,
  output [15:0] out_3
);

  wire [1:0] rmv2_1_lower2;
  wire [3:0] rmv4_1_lower4;
  wire [7:0] multiplexer_2_out, rmv8_1_lower8;
  wire [11:0] multiplexer_4_out;
  wire [13:0] multiplexer_6_out;
  wire [14:0] multiplexer_8_out;
  wire [14:14] rmv1_1_lower1;
  wire [15:0] multiplexer_1_out, multiplexer_3_out, multiplexer_5_out, multiplexer_7_out, rmv1_1_upper15,
       rmv2_1_upper14, rmv4_1_upper12, rmv8_1_upper8;

  Rmv8 rmv8_1 (.in_1(in_2), .Lower8(rmv8_1_lower8), .Upper8(rmv8_1_upper8));
  Multiplexer #(.width(16)) multiplexer_1 (
    .in0(in_2), .in1(rmv8_1_upper8), .out(multiplexer_1_out), .sel(in_1[3]));  // open: en
  Multiplexer #(.width(8)) multiplexer_2 (
    .in0({8{1'b0}}), .in1(rmv8_1_lower8), .out(multiplexer_2_out), .sel(in_1[3]));  // open: en
  Rmv4 rmv4_1 (.in_1(multiplexer_1_out), .Lower4(rmv4_1_lower4), .Upper12(rmv4_1_upper12));
  Multiplexer #(.width(16)) multiplexer_3 (
    .in0(multiplexer_1_out), .in1(rmv4_1_upper12), .out(multiplexer_3_out), .sel(in_1[2]));  // open: en
  Multiplexer #(.width(12)) multiplexer_4 (
    .in0({multiplexer_2_out, 4'b0000}), .in1({rmv4_1_lower4, multiplexer_2_out}), .out(multiplexer_4_out),
    .sel(in_1[2]));  // open: en
  Multiplexer #(.width(16)) multiplexer_5 (
    .in0(multiplexer_3_out), .in1(rmv2_1_upper14), .out(multiplexer_5_out), .sel(in_1[1]));  // open: en
  Rmv2 rmv2_1 (.in_1(multiplexer_3_out), .Lower2(rmv2_1_lower2), .Upper14(rmv2_1_upper14));
  Rmv1 rmv1_1 (.in_1(multiplexer_5_out), .Lower1(rmv1_1_lower1[14]), .Upper15(rmv1_1_upper15));
  Multiplexer #(.width(14)) multiplexer_6 (
    .in0({multiplexer_4_out, 2'b00}), .in1({rmv2_1_lower2, multiplexer_4_out}), .out(multiplexer_6_out),
    .sel(in_1[1]));  // open: en
  Multiplexer #(.width(16)) multiplexer_7 (
    .in0(multiplexer_5_out), .in1(rmv1_1_upper15), .out(multiplexer_7_out), .sel(in_1[0]));  // open: en
  Multiplexer #(.width(15)) multiplexer_8 (
    .in0({multiplexer_6_out, 1'b0}), .in1({rmv1_1_lower1[14], multiplexer_6_out}), .out(multiplexer_8_out),
    .sel(in_1[0]));  // open: en
  assign out_3 = multiplexer_7_out | {multiplexer_8_out, 1'b0};  // OR_Gate or_1, 16 bits wide
endmodule

module Rmv8 (
  input  [15:0] in_1,
  output [7:0] Lower8,
  output [15:0] Upper8
);


  assign Lower8 = in_1[7:0];
  assign Upper8 = {{8{1'b0}}, in_1[15:8]};
endmodule

module Rmv4 (
  input  [15:0] in_1,
  output [3:0] Lower4,
  output [15:0] Upper12
);


  assign Lower4 = in_1[3:0];
  assign Upper12 = {4'b0000, in_1[15:4]};
endmodule

module Rmv2 (
  input  [15:0] in_1,
  output [1:0] Lower2,
  output [15:0] Upper14
);


  assign Lower2 = in_1[1:0];
  assign Upper14 = {2'b00, in_1[15:2]};
endmodule

module Rmv1 (
  input  [15:0] in_1,
  output Lower1,
  output [15:0] Upper15
);


  assign Lower1 = in_1[0];
  assign Upper15 = {1'b0, in_1[15:1]};
endmodule
